// Logisim project SequentialDivider.circ as structural Verilog: 1 circuit, main circuit Divider
module Divider (
  input  [3:0] Dividend,
  input  [3:0] Divisor,
  input  RESET,
  output [3:0] Quotient,
  output [3:0] Remainder,
  output DONE
);

  wire and_1_out, and_2_out, and_3_out, and_4_out, and_5_out, CHECKER1, CHECKER2, CLOCK, not_1_out,
       not_2_out, not_3_out, not_4_out, not_5_out, not_6_out, not_9_out, subtractor_1_bout;
  wire [2:0] counter_1_q, counter_2_q;
  wire [7:0] multiplexer_1_out, multiplexer_2_out, shift_register_1_p20, subtractor_1_out;
  wire [7:4] register_1_q;

  Clock clock_1 (.out(CLOCK));
  not not_1 (not_1_out, Divisor[0]);
  not not_2 (not_2_out, Divisor[1]);
  and and_1 (and_1_out, not_1_out, not_2_out, not_3_out, not_4_out);
  not not_3 (not_3_out, Divisor[2]);
  not not_4 (not_4_out, Divisor[3]);
  not not_5 (not_5_out, CHECKER1);
  or or_1 (DONE, and_1_out, not_5_out);
  // Probe on Divisor
  and and_2 (and_2_out, CLOCK, CHECKER2);
  // Shift_Register shift_register_1: pin names not known; wires that end beside it: RESET, 1'b1, and_2_out, 1'b0, Divisor[3], Divisor[2], Divisor[1], Divisor[0], 1'b0, 1'b0, 1'b0, 1'b0, shift_register_1_p20[7], shift_register_1_p20[6], shift_register_1_p20[5], shift_register_1_p20[4], shift_register_1_p20[3], shift_register_1_p20[2], shift_register_1_p20[1], shift_register_1_p20[0]
  Counter #(.width(3), .max('h5)) counter_1 (
    .clr(RESET), .load(RESET), .up(1'b1), .count(CHECKER1), .clk(CLOCK), .D(3'b000), .Q(counter_1_q));  // open: carry
  // Probe on shift_register_1_p20
  and and_3 (and_3_out, CLOCK, CHECKER1);
  not not_6 (not_6_out, subtractor_1_bout);
  Subtractor subtractor_1 (
    .a({register_1_q, Remainder}), .b(shift_register_1_p20), .out(subtractor_1_out), .bout(subtractor_1_bout));  // open: bin
  Multiplexer #(.width(8), .enable("false")) multiplexer_1 (
    .in0(subtractor_1_out), .in1({register_1_q, Remainder}), .out(multiplexer_1_out), .sel(subtractor_1_bout));
  not not_7 (CHECKER1, and_4_out);
  and and_4 (and_4_out, counter_1_q[0], counter_1_q[2]);
  // Shift_Register #(.length(4)) shift_register_2: pin names not known; wires that end beside it: RESET, 1'b1, and_3_out, not_6_out, 1'b0, 1'b0, 1'b0, 1'b0, Quotient[0], Quotient[1], Quotient[2], Quotient[3]
  Multiplexer #(.width(8), .enable("false")) multiplexer_2 (
    .in0(multiplexer_1_out), .in1({4'b0000, Dividend}), .out(multiplexer_2_out), .sel(RESET));
  Register register_1 (.D(multiplexer_2_out), .en(1'b1), .clk(CLOCK), .Q({register_1_q, Remainder}));  // open: clr
  Counter #(.width(3), .max('h5)) counter_2 (
    .clr(RESET), .load(RESET), .up(1'b1), .count(CHECKER2), .clk(CLOCK), .D(3'b000), .Q(counter_2_q));  // open: carry
  // Probe on Quotient
  // Probe on {register_1_q, Remainder}
  not not_8 (CHECKER2, and_5_out);
  and and_5 (and_5_out, not_9_out, counter_2_q[2]);
  not not_9 (not_9_out, counter_2_q[0]);
  // also tied to GND on the sheet: {register_1_q[4], register_1_q[5], register_1_q[6], register_1_q[7]}

  // Other names for the same wires on the sheet: RMD[3:0] = Remainder; QUO[3:0] = Quotient

  // Notes on the sheet:
  //   GREG WOO, 260777364
endmodule
