// Logisim project SequentialMultipler.circ as structural Verilog: 1 circuit, main circuit Multiplier
module Multiplier (
  input  [3:0] A,
  input  [3:0] B,
  input  RESET,
  output [7:0] PRODUCT,
  output DONE
);

  wire CLOCK, LSB, not_1_out, not_2_out, not_3_out, not_4_out, or_1_out, shift_register_2_p9,
       shift_register_2_p10, shift_register_2_p11;
  wire [7:0] adder_1_out, multiplexer_1_out, shift_register_1_p13;

  // Probe on A
  Clock #(.highDuration(2)) clock_1 (.out(CLOCK));
  // Shift_Register shift_register_1: pin names not known; wires that end beside it: RESET, 1'b1, CLOCK, 1'b0, A[0], A[1], A[2], A[3], 1'b0, 1'b0, 1'b0, 1'b0, shift_register_1_p13[0], shift_register_1_p13[1], shift_register_1_p13[2], shift_register_1_p13[3], shift_register_1_p13[4], shift_register_1_p13[5], shift_register_1_p13[6], shift_register_1_p13[7]
  // Probe on PRODUCT
  // Probe on B
  // Shift_Register #(.length(4)) shift_register_2: pin names not known; wires that end beside it: RESET, 1'b1, CLOCK, 1'b0, B[3], B[2], B[1], B[0], shift_register_2_p9, shift_register_2_p10, shift_register_2_p11, LSB
  Adder adder_1 (.a(shift_register_1_p13), .b(PRODUCT), .out(adder_1_out));  // open: cin, cout
  Multiplexer #(.width(8), .enable("false")) multiplexer_1 (
    .in0(adder_1_out), .in1({8{1'b0}}), .out(multiplexer_1_out), .sel(RESET));
  or or_1 (or_1_out, LSB, RESET);
  Register register_1 (.D(multiplexer_1_out), .en(or_1_out), .clk(CLOCK), .Q(PRODUCT));  // open: clr
  not not_1 (not_1_out, shift_register_2_p9);
  not not_2 (not_2_out, shift_register_2_p10);
  not not_3 (not_3_out, shift_register_2_p11);
  not not_4 (not_4_out, LSB);
  and and_1 (DONE, not_1_out, not_2_out, not_3_out, not_4_out);

  // Notes on the sheet:
  //   GREG WOO, 260777364
endmodule
